// Logisim project DATAPATH.circ as structural Verilog: 2 circuits, main circuit DataPath
module DataPath (
  input  [31:0] Input_Value,
  input  CLK,
  output [23:0] Index_Memory,
  output [23:0] Index_Input,
  output [31:0] Memory_Value,
  output resto____0
);

  wire L_divisor, L_Index_Input, L_Index_Memory, L_int_div, L_int_non_div, L_size, L_value, pos____size;
  wire [23:0] Index_Input___1, int_non_div_size, multiplexer_1_out, multiplexer_2_out, size, size_1;
  wire [31:0] divisor, int_div, int_div_1, int_non_div, int_non_div_1, pos, pos_1, value___divisor;

  // Probe on int_div
  Register #(.width(32)) u_int_div (.D(int_div_1), .en(L_int_div), .Q(int_div), .clk(CLK));  // open: clr
  // Probe on int_non_div
  Register #(.width(32)) int_div_2 (.D(int_non_div_1), .en(L_int_non_div), .Q(int_non_div), .clk(CLK));  // open: clr
  // Probe on size
  Register #(.width(24)) u_size (.D(Input_Value[23:0]), .en(L_size), .Q(size), .clk(CLK));  // open: clr
  Register #(.width(32)) u_divisor (.D(Input_Value), .en(L_divisor), .Q(divisor), .clk(CLK));  // open: clr
  // Probe on divisor
  // Probe on Memory_Value
  Register #(.width(32)) value (.D(Input_Value), .en(L_value), .Q(Memory_Value), .clk(CLK));  // open: clr
  Multiplexer #(.width(24)) multiplexer_1 (
    .in0(int_div[23:0]), .in1(int_non_div_size), .out(multiplexer_1_out));  // open: sel, en
  Multiplexer #(.select(2), .width(24)) multiplexer_2 (
    .in0(size_1), .in1(24'h1), .in2(Index_Input___1), .out(multiplexer_2_out));  // open: in3, sel, en
  // Probe on Index_Memory
  Register #(.width(24)) u_Index_Memory (
    .D(multiplexer_1_out), .en(L_Index_Memory), .Q(Index_Memory), .clk(CLK));  // open: clr
  // Probe on Index_Input
  Register #(.width(24)) u_Index_Input (
    .D(multiplexer_2_out), .en(L_Index_Input), .Q(Index_Input), .clk(CLK));  // open: clr
  Adder #(.width(32)) adder_1 (.a(int_div), .b(32'h1), .out(int_div_1));  // open: cin, cout
  Adder #(.width(32)) adder_2 (.a(int_non_div), .b(32'h1), .out(int_non_div_1));  // open: cin, cout
  Adder #(.width(32)) adder_3 (.a(pos), .b(32'h1), .out(pos_1));  // open: cin, cout
  Adder #(.width(24)) adder_4 (.a(size), .b(24'h1), .out(size_1));  // open: cin, cout
  Comparator #(.width(24)) comparator_1 (.a(Index_Input), .b(size), .eq(pos____size));  // open: gt, lt
  Divider #(.width(32)) divider_1 (.a(Memory_Value), .b(divisor), .rem(value___divisor));  // open: out, upper
  Comparator #(.width(32)) comparator_2 (.a(value___divisor), .b({32{1'b0}}), .eq(resto____0));  // open: gt, lt

  // Other names for the same wires on the sheet: value[31:0] = Memory_Value
endmodule

module ControlUnit (
  input  START,
  input  CLK,
  input  II___size,
  input  resto____0,
  output END,
  output Write,
  output Ls,
  output Lv,
  output Ld,
  output L_id,
  output L_ind,
  output L_IM,
  output L_II,
  output S_IM,
  output S_II0,
  output S_II1
);

  wire b____0, d_ff_1_q, d_ff_2_q, demultiplexer_1_out0, La0, La1, Lb0, or_1_out, RESET, WHILE_q;

  D_Flip_Flop d_ff_1 (.clk(CLK), .D(START), .Q(d_ff_1_q));  // open: Qn, preset, en, reset
  Demultiplexer #(.enable("false")) demultiplexer_1 (
    .out0(demultiplexer_1_out0), .out1(Lb0), .in(d_ff_2_q), .sel(START));
  D_Flip_Flop d_ff_2 (.clk(CLK), .D(demultiplexer_1_out0), .Q(d_ff_2_q), .preset(RESET));  // open: Qn, en, reset
  xor xor_1 (RESET, START, d_ff_1_q);
  D_Flip_Flop d_ff_3 (.clk(CLK), .D(Lb0), .Q(La0), .reset(RESET));  // open: Qn, preset, en
  or or_1 (or_1_out, La0, La1);
  D_Flip_Flop WHILE (.clk(CLK), .D(or_1_out), .Q(WHILE_q), .reset(RESET));  // open: Qn, preset, en
  Demultiplexer #(.enable("false")) demultiplexer_2 (.out0(END), .out1(La1), .in(WHILE_q), .sel(b____0));

  // Other names for the same wires on the sheet: Lb1 = La0; Sb0 = La0; Lb2 = La1; Sa = La1; Sb1 = La1
endmodule
